// Logisim project ex1.circ as structural Verilog: 5 circuits, main circuit NAND1
module NAND1 (
  input  A,
  input  B,
  output RESULT
);

  wire not_1_out, not_2_out;

  not not_1 (not_1_out, A);
  not not_2 (not_2_out, B);
  or or_1 (RESULT, not_1_out, not_2_out);

  // Notes on the sheet:
  //   PUT CIRCUITRY HERE
endmodule

module NOR1 (
  input  A,
  input  B,
  output RESULT
);

  wire not_1_out, not_2_out;

  not not_1 (not_1_out, A);
  not not_2 (not_2_out, B);
  and and_1 (RESULT, not_1_out, not_2_out);

  // Notes on the sheet:
  //   PUT CIRCUITRY HERE
endmodule

module XOR1 (
  input  A,
  input  B,
  output RESULT
);

  wire and_1_out, not_1_out, or_1_out;

  and and_1 (and_1_out, A, B);
  not not_1 (not_1_out, and_1_out);
  or or_1 (or_1_out, A, B);
  and and_2 (RESULT, not_1_out, or_1_out);

  // Notes on the sheet:
  //   PUT CIRCUITRY HERE
endmodule

module MUX2 (
  input  A,
  input  B,
  input  Sel,
  output RESULT
);

  wire and_1_out, and_2_out, not_1_out;

  not not_1 (not_1_out, Sel);
  and and_1 (and_1_out, A, not_1_out);
  and and_2 (and_2_out, B, Sel);
  or or_1 (RESULT, and_1_out, and_2_out);

  // Notes on the sheet:
  //   PUT CIRCUITRY HERE
endmodule

module MUX4 (
  input  A,
  input  B,
  input  C,
  input  D,
  input  Sel1,
  input  Sel2,
  output RESULT
);

  wire and_1_out, and_2_out, and_3_out, and_4_out, and_5_out, and_6_out, not_1_out, not_2_out, not_3_out,
       or_1_out, or_2_out;

  not not_1 (not_1_out, Sel1);
  not not_2 (not_2_out, Sel1);
  and and_1 (and_1_out, not_1_out, A);
  and and_2 (and_2_out, Sel1, B);
  and and_3 (and_3_out, not_2_out, C);
  and and_4 (and_4_out, Sel1, D);
  or or_1 (or_1_out, and_1_out, and_2_out);
  not not_3 (not_3_out, Sel2);
  or or_2 (or_2_out, and_3_out, and_4_out);
  and and_5 (and_5_out, not_3_out, or_1_out);
  and and_6 (and_6_out, Sel2, or_2_out);
  or or_3 (RESULT, and_5_out, and_6_out);

  // Notes on the sheet:
  //   PUT CIRCUITRY HERE
endmodule
