// Logisim project ex5.circ as structural Verilog: 6 circuits, main circuit rotr
module rotr (
  input  [15:0] A,
  input  [3:0] B,
  output [15:0] Out1
);

  wire [15:0] mux_1_out_4, mux_2_out_4, mux_3_out_4, rot1_1_out_2, rot2_1_out_2, rot4_1_out_2, rot8_1_out_2;

  rot1 rot1_1 (.in_1(A), .out_2(rot1_1_out_2));
  mux mux_1 (.out_4(mux_1_out_4), .in_3(B[0]), .in_1(A), .in_2(rot1_1_out_2));
  rot2 rot2_1 (.in_1(mux_1_out_4), .out_2(rot2_1_out_2));
  mux mux_2 (.out_4(mux_2_out_4), .in_3(B[1]), .in_1(mux_1_out_4), .in_2(rot2_1_out_2));
  rot4 rot4_1 (.in_1(mux_2_out_4), .out_2(rot4_1_out_2));
  mux mux_3 (.out_4(mux_3_out_4), .in_3(B[2]), .in_1(mux_2_out_4), .in_2(rot4_1_out_2));
  rot8 rot8_1 (.in_1(mux_3_out_4), .out_2(rot8_1_out_2));
  mux mux_4 (.out_4(Out1), .in_3(B[3]), .in_1(mux_3_out_4), .in_2(rot8_1_out_2));

  // Notes on the sheet:
  //   PUT CIRCUITRY HERE
endmodule

module rot8 (
  input  [15:0] in_1,
  output [15:0] out_2
);


  assign out_2 = {in_1[7:0], in_1[15:8]};

  // Notes on the sheet:
  //   PUT CIRCUITRY HERE
endmodule

module rot4 (
  input  [15:0] in_1,
  output [15:0] out_2
);


  assign out_2 = {in_1[3:0], in_1[15:4]};

  // Notes on the sheet:
  //   PUT CIRCUITRY HERE
endmodule

module rot2 (
  input  [15:0] in_1,
  output [15:0] out_2
);


  assign out_2 = {in_1[1:0], in_1[15:2]};

  // Notes on the sheet:
  //   PUT CIRCUITRY HERE
endmodule

module rot1 (
  input  [15:0] in_1,
  output [15:0] out_2
);


  assign out_2 = {in_1[0], in_1[15:1]};

  // Notes on the sheet:
  //   PUT CIRCUITRY HERE
endmodule

module mux (
  input  [15:0] in_1,
  input  [15:0] in_2,
  input  in_3,
  output [15:0] out_4
);

  wire not_1_out;
  wire [15:0] and_1_out, and_2_out, bit_extender_1_out, bit_extender_2_out;

  not not_1 (not_1_out, in_3);
  assign bit_extender_1_out = {{15{not_1_out}}, not_1_out};  // Bit_Extender bit_extender_1
  assign bit_extender_2_out = {{15{in_3}}, in_3};  // Bit_Extender bit_extender_2
  assign and_1_out = in_1 & bit_extender_1_out;  // AND_Gate and_1, 16 bits wide
  assign and_2_out = in_2 & bit_extender_2_out;  // AND_Gate and_2, 16 bits wide
  assign out_4 = and_1_out | and_2_out;  // OR_Gate or_1, 16 bits wide
endmodule
