// Logisim project alu.circ as structural Verilog: 1 circuit, main circuit alu
module alu (
  input  [31:0] A,
  input  [31:0] B,
  input  [3:0] ALUSel,
  output [31:0] Result
);

  wire comparator_1_lt;
  wire [4:0] bit_extender_1_out, bit_extender_2_out, bit_extender_3_out;
  wire [31:0] a0, a1, a2, a3, a4, a5, a6, a7, a10, a11, a12, a14, multiplier_1_out;
  wire [63:0] bit_extender_4_out, bit_extender_5_out, bit_extender_6_out, bit_extender_7_out;

  Bit_Extender #(.in_width(32), .out_width(5)) bit_extender_1 (.in(B), .out(bit_extender_1_out));
  Bit_Extender #(.in_width(32), .out_width(5)) bit_extender_2 (.in(B), .out(bit_extender_2_out));
  Bit_Extender #(.in_width(32), .out_width(5)) bit_extender_3 (.in(B), .out(bit_extender_3_out));
  assign bit_extender_4_out = {{32{1'b0}}, A};  // Bit_Extender bit_extender_4
  assign bit_extender_5_out = {{32{1'b0}}, B};  // Bit_Extender bit_extender_5
  assign bit_extender_6_out = {{32{A[31]}}, A};  // Bit_Extender bit_extender_6
  assign bit_extender_7_out = {{32{B[31]}}, B};  // Bit_Extender bit_extender_7
  Adder #(.width(32)) adder_1 (.a(A), .b(B), .out(a0));  // open: cin, cout
  Subtractor #(.width(32)) subtractor_1 (.a(A), .b(B), .out(a12));  // open: bin, bout
  assign a1 = A & B;  // AND_Gate and_1, 32 bits wide
  assign a2 = A | B;  // OR_Gate or_1, 32 bits wide
  assign a3 = A ^ B;  // XOR_Gate xor_1, 32 bits wide
  Shifter #(.shift("lr"), .width(32)) shifter_1 (.in(A), .\dist (bit_extender_1_out), .out(a4));
  Shifter #(.shift("ar"), .width(32)) shifter_2 (.in(A), .\dist (bit_extender_2_out), .out(a5));
  Shifter #(.width(32)) shifter_3 (.in(A), .\dist (bit_extender_3_out), .out(a6));
  Comparator #(.width(32)) comparator_1 (.a(A), .b(B), .lt(comparator_1_lt));  // open: gt, eq
  Multiplier #(.width(64)) multiplier_1 (
    .a(bit_extender_4_out), .b(bit_extender_5_out), .out({a11, multiplier_1_out}));  // open: cin, cout
  Multiplier #(.mode("twosComplement"), .width(64)) multiplier_2 (
    .a(bit_extender_6_out), .b(bit_extender_7_out), .out({a14, a10}));  // open: cin, cout
  assign a7 = {{31{1'b0}}, comparator_1_lt};  // Bit_Extender bit_extender_8
  Multiplexer #(.enable("false"), .select(4), .width(32)) multiplexer_1 (
    .in0(a0), .in1(a1), .in2(a2), .in3(a3), .in4(a4), .in5(a5), .in6(a6), .in7(a7), .in10(a10), .in11(a11),
    .in12(a12), .in13(B), .in14(a14), .out(Result), .sel(ALUSel));  // open: in8, in9, in15

  // Notes on the sheet:
  //   INPUTS to your circuit
  //   DON'T CHANGE THE LOCATIONS OF THE INPUTS AND OUTPUTS!
  //   OUTPUT from your circuit
endmodule
