// Logisim project control_logic.circ as structural Verilog: 1 circuit, main circuit control_logic
module control_logic (
  input  [31:0] inst,
  input  BrEq,
  input  BrLt,
  output PCSel,
  output RegWEn,
  output [2:0] ImmSel,
  output BrUn,
  output ASel,
  output BSel,
  output [3:0] ALUSel,
  output MemRW,
  output [1:0] WBSel,
  output CSRSel,
  output CSRWen
);

  Comparator #(.width(7)) comparator_1 (.a(inst[6:0]), .b(7'b0110011));  // open: gt, eq, lt
  Comparator #(.width(7)) comparator_2 (.a(inst[6:0]), .b(7'b0000011));  // open: gt, eq, lt
  Comparator #(.width(7)) comparator_3 (.a(inst[6:0]), .b(7'b0010011));  // open: gt, eq, lt
  Comparator #(.width(7)) comparator_4 (.a(inst[6:0]), .b(7'b0100011));  // open: gt, eq, lt
  Comparator #(.width(7)) comparator_5 (.a(inst[6:0]), .b(7'b1100011));  // open: gt, eq, lt
  Comparator #(.width(7)) comparator_6 (.a(inst[6:0]), .b(7'b0010111));  // open: gt, eq, lt
  Comparator #(.width(7)) comparator_7 (.a(inst[6:0]), .b(7'b0110111));  // open: gt, eq, lt
  Comparator #(.width(7)) comparator_8 (.a(inst[6:0]), .b(7'b1101111));  // open: gt, eq, lt
  Comparator #(.width(7)) comparator_9 (.a(inst[6:0]), .b(7'b1100111));  // open: gt, eq, lt
  Comparator #(.width(7)) comparator_10 (.a(inst[6:0]), .b(7'b1110011));  // open: gt, eq, lt
  ROM #(.addrWidth(7), .dataWidth(14)) rom_1 ();  // open: addr, data

  // Other names for the same wires on the sheet: opcode[6:0] = inst[6:0]; func3[2:0] = inst[14:12];
  //   func7[6:0] = inst[31:25]

  // Notes on the sheet:
  //   INPUTS to your circuit
  //   DON'T CHANGE THE LOCATIONS OF THE INPUTS AND OUTPUTS!
  //   OUTPUT from your circuit
endmodule
